# Fritzing sketch watering (saved by Fritzing 0.9.10b)
breadboards: 1

parts:
  Pico_H1 = Raspberry Pi Pico H
  LED1 = smd LED [color="Red (633nm)" package="0805 [SMD]"]
  Chirp!_Soil_Moisture_Sensor1 = Chirp! Soil Moisture Sensor v2.7.3
  R1 = Resistor [tolerance=±5% power=0.25 resistance=220 package=THT]
  S1 = Momentary Switch [package=ksa_sealed_tac_switch]
  U4 = TRANSISTOR_NPN_2 [package=to-92]
  D1 = Rectifier Diode [part_number=1N4001 package="300 mil [THT]"]
  M1 = DC Motor [voltage_(max)=6V voltage_(min)=3V]
  U5 = RELAY-2 [package=relay-g5v]
  D2 = Rectifier Diode [part_number=1N4001 package="300 mil [THT]"]
  R2 = Resistor [tolerance=±5% power=0.25 resistance=6 package=THT]
  R3 = Resistor [tolerance=±5% power=0.25 resistance=20000 package=THT]
  R4 = Resistor [tolerance=±5% power=0.25 resistance=20000 package=THT]
  R5 = Rotary Potentiometer (Large) [maximum_resistance=100kΩ knob_status=50% power=0.5W package=THT]
  JP1 = USB_MICROB_PLUG [package=micro-b-th]

nets:
  N1: Pico_H1.VSYS, Chirp!_Soil_Moisture_Sensor1.Pin_1, U4.C, U5.6, JP1.VCC
  GND: Pico_H1.GND, Chirp!_Soil_Moisture_Sensor1.pin_5, S1.2, JP1.GND
  N2: Pico_H1.3V3, R4.Pin_0, R5.leg1
  N3: Pico_H1.GP27_A1, R5.wiper
  N4: Pico_H1.GP26_A0, Chirp!_Soil_Moisture_Sensor1.pin_4
  N5: Pico_H1.GP22, R3.Pin_0, R5.leg2
  N6: Pico_H1.GP16, U4.B
  N7: LED1.cathode, D1.anode, M1.pin_1, U5.2, D2.anode
  N8: LED1.anode, R1.Pin_0
  N9: R1.Pin_1, U4.E, D1.cathode, U5.9
  N10: S1.3, R3.Pin_1
  N11: S1.4, R4.Pin_1
  N12: M1.pin_2, D2.cathode, R2.Pin_1
  N13: U5.10, R2.Pin_0

custom parts:
  Raspberry Pi Pico H: Raspberry Pi Pico H. Based around the RP2040 microcontroller the Pico H is a low cost microcontroller device bringing Raspberry Pi quality, cost, and easy of use to the microcontroller space.
  RELAY-2: SPDT relay (COM-00100)
