# Fritzing sketch watering_new_architecture (saved by Fritzing 0.9.10b)
circuit board: 8.46667cm x 5.64444cm
breadboards: 1

parts:
  Pico_H1 = Raspberry Pi Pico H
  LED1 = smd LED [color="Red (633nm)" package="0805 [SMD]"]
  Soil_Moisture_Sensor1 = Chirp! Soil Moisture Sensor v2.7.3
  R1 = Resistor [tolerance=±5% power=0.25 resistance=220 package=THT]
  U4 = TRANSISTOR_NPN_2 [package=to-92]
  D1 = Rectifier Diode [part_number=1N4001 package="300 mil [THT]"]
  M1 = DC Motor [voltage_(max)=6V voltage_(min)=3V]
  U5 = RELAY-2 [package=relay-g5v]
  D2 = Rectifier Diode [part_number=1N4001 package="300 mil [THT]"]
  R2 = Resistor [tolerance=±5% power=0.25 resistance=6 package=THT]
  JP1 = USB_MICROB_PLUG [package=micro-b-th]
  S2 = Pushbutton [package="[THT]"]
  S3 = Pushbutton [package="[THT]"]
  S4 = Pushbutton [package="[THT]"]
  S5 = Pushbutton [package="[THT]"]
  R8 = Resistor [tolerance=±5% power=0.25 resistance=22k package=THT]
  R9 = Resistor [tolerance=±5% power=0.25 resistance=22k package=THT]
  R10 = Resistor [tolerance=±5% power=0.25 resistance=22k package=THT]
  R11 = Resistor [tolerance=±5% power=0.25 resistance=22k package=THT]

nets (from the schematic view):
  N1: Pico_H1.VSYS, Soil_Moisture_Sensor1.Pin_1, U4.C, U5.6, JP1.VCC
  GND: Pico_H1.GND, Soil_Moisture_Sensor1.pin_5, JP1.GND, S2.Pin_2, S3.Pin_1, S3.Pin_2, S4.Pin_1, S4.Pin_2, S5.Pin_1, S5.Pin_2
  N2: Pico_H1.3V3_EN, R8.Pin_0, R9.Pin_0, R10.Pin_0, R11.Pin_0
  N3: Pico_H1.GP26_A0, Soil_Moisture_Sensor1.pin_4
  N4: Pico_H1.GP16, U4.B
  N5: Pico_H1.GP5, S5.Pin_3, S5.Pin_4, R11.Pin_1
  N6: Pico_H1.GP4, S4.Pin_3, S4.Pin_4, R10.Pin_1
  N7: Pico_H1.GP3, S3.Pin_3, S3.Pin_4, R9.Pin_1
  N8: Pico_H1.GP2, S2.Pin_3, S2.Pin_4, R8.Pin_1
  N9: LED1.cathode, D1.anode, M1.pin_1, U5.2, D2.anode
  N10: LED1.anode, R1.Pin_0
  N11: R1.Pin_1, U4.E, D1.cathode, U5.9
  N12: M1.pin_2, D2.cathode, R2.Pin_1
  N13: U5.10, R2.Pin_0

custom parts:
  Raspberry Pi Pico H: Raspberry Pi Pico H. Based around the RP2040 microcontroller the Pico H is a low cost microcontroller device bringing Raspberry Pi quality, cost, and easy of use to the microcontroller space.
  RELAY-2: SPDT relay (COM-00100)
